# Fritzing sketch 2xLDR (saved by Fritzing 0.9.3b)
breadboards: 1

parts:
  LDR_2 = Photocell (LDR) [package=THT]
  part = Resistor [tolerance=±5% resistance=100k package="2512 [SMD]"]
  part_2 = Resistor [tolerance=±5% resistance=100k package="2512 [SMD]"]
  LDR_1 = Photocell (LDR) [package=THT]
  J1 = Dagu DGServo 9g header (male) [package=THT]
  part_3 = Dagu DGServo 9g header (male) [package=THT]

nets:
  N1: LDR_2.pin_0, part.Pin_1, J1.pulse
  N2: LDR_2.pin_1, J1.Vcc
  N3: part.Pin_0, J1.gnd
  N4: part_2.Pin_0, LDR_1.pin_1, part_3.pulse
  N5: part_2.Pin_1, part_3.gnd
  N6: LDR_1.pin_0, part_3.Vcc

notes:
  GND
  VCC
  S1
  SLOT 1
  GND
  Vcc
  S2
  SLOT 2
