# Fritzing sketch LDR (saved by Fritzing 0.9.3b)
breadboards: 1

parts:
  part = Resistor [tolerance=±5% resistance=100k package="2512 [SMD]"]
  LDR_1 = Photocell (LDR) [package=THT]
  part_2 = Dagu DGServo 9g header (male) [package=THT]

nets:
  N1: part.Pin_0, LDR_1.pin_1, part_2.pulse
  N2: part.Pin_1, part_2.gnd
  N3: LDR_1.pin_0, part_2.Vcc

notes:
  GND
  Vcc
  S1
  SLOT 1
